# Fritzing sketch not7segwithdes (saved by Fritzing 0.9.3b)
breadboards: 63

parts:
  IC2 = IC, DIP package, 14 pins [chip_label=7404]
  IC3 = IC, DIP package, 14 pins [chip_label=7404]
  S1 = Toggle Switch [package=THT]
  S2 = Toggle Switch [package=THT]
  S3 = Toggle Switch [package=THT]
  S4 = Toggle Switch [package=THT]
  IC5 = 4081 4 x 2 Input AND Gate, multi-part [part_number=4081 package="DIP (Dual Inline) [THT]"]
  IC5_1 = 4081_4_x_2_input_AND_gate_multipart_subpart2 [part_number=4081]  # not connected
  IC5_2 = 4081_4_x_2_input_AND_gate_multipart_subpart3 [part_number=4081]  # not connected
  IC7_4 = 4081_4_x_2_input_AND_gate_multipart_subpart5 [part_number=4081]  # not connected
  IC7_2 = 4081_4_x_2_input_AND_gate_multipart_subpart3 [part_number=4081]  # not connected
  IC7 = 4081 4 x 2 Input AND Gate, multi-part [part_number=4081 package="DIP (Dual Inline) [THT]"]
  IC9_4 = 4081_4_x_2_input_AND_gate_multipart_subpart5 [part_number=4081]  # not connected
  부품3 = 4081_4_x_2_input_AND_gate_multipart_subpart1 [part_number=4081]  # not connected
  IC9 = 4081 4 x 2 Input AND Gate, multi-part [part_number=4081 package="DIP (Dual Inline) [THT]"]
  IC9_1 = 4081_4_x_2_input_AND_gate_multipart_subpart2 [part_number=4081]  # not connected
  IC10 = 4071 4 x 2 Input OR Gate, multi-part [part_number=4071 package="DIP (Dual Inline) [THT]"]
  부품4 = 4071_4_x_2_input_OR_gate_multipart_subpart1 [part_number=4071]  # not connected
  IC10_1 = 4071_4_x_2_input_OR_gate_multipart_subpart2 [part_number=4071]  # not connected
  IC10_2 = 4071_4_x_2_input_OR_gate_multipart_subpart3 [part_number=4071]  # not connected
  IC10_4 = 4071_4_x_2_input_OR_gate_multipart_subpart5 [part_number=4071]  # not connected
  IC11_3 = 4071_4_x_2_input_OR_gate_multipart_subpart4 [part_number=4071]  # not connected
  IC11_4 = 4071_4_x_2_input_OR_gate_multipart_subpart5 [part_number=4071]  # not connected
  IC11_2 = 4071_4_x_2_input_OR_gate_multipart_subpart3 [part_number=4071]  # not connected
  부품5 = 4071_4_x_2_input_OR_gate_multipart_subpart1 [part_number=4071]  # not connected
  IC11 = 4071 4 x 2 Input OR Gate, multi-part [part_number=4071 package="DIP (Dual Inline) [THT]"]
  IC11_1 = 4071_4_x_2_input_OR_gate_multipart_subpart2 [part_number=4071]  # not connected
  IC12_3 = 4071_4_x_2_input_OR_gate_multipart_subpart4 [part_number=4071]  # not connected
  IC12_2 = 4071_4_x_2_input_OR_gate_multipart_subpart3 [part_number=4071]  # not connected
  IC12_4 = 4071_4_x_2_input_OR_gate_multipart_subpart5 [part_number=4071]  # not connected
  IC12 = 4071 4 x 2 Input OR Gate, multi-part [part_number=4071 package="DIP (Dual Inline) [THT]"]
  IC12_1 = 4071_4_x_2_input_OR_gate_multipart_subpart2 [part_number=4071]  # not connected
  IC13_3 = 4071_4_x_2_input_OR_gate_multipart_subpart4 [part_number=4071]  # not connected
  IC13_4 = 4071_4_x_2_input_OR_gate_multipart_subpart5 [part_number=4071]  # not connected
  IC13_2 = 4071_4_x_2_input_OR_gate_multipart_subpart3 [part_number=4071]  # not connected
  IC13 = 4071 4 x 2 Input OR Gate, multi-part [part_number=4071 package="DIP (Dual Inline) [THT]"]
  IC13_1 = 4071_4_x_2_input_OR_gate_multipart_subpart2 [part_number=4071]  # not connected
  IC14_1 = 4071_4_x_2_input_OR_gate_multipart_subpart2 [part_number=4071]  # not connected
  부품8 = 4071_4_x_2_input_OR_gate_multipart_subpart1 [part_number=4071]  # not connected
  IC14_4 = 4071_4_x_2_input_OR_gate_multipart_subpart5 [part_number=4071]  # not connected
  IC14 = 4071 4 x 2 Input OR Gate, multi-part [part_number=4071 package="DIP (Dual Inline) [THT]"]
  IC14_2 = 4071_4_x_2_input_OR_gate_multipart_subpart3 [part_number=4071]  # not connected
  IC15_4 = 4081_4_x_2_input_AND_gate_multipart_subpart5 [part_number=4081]  # not connected
  IC15 = 4081 4 x 2 Input AND Gate, multi-part [part_number=4081 package="DIP (Dual Inline) [THT]"]
  IC15_3 = 4081_4_x_2_input_AND_gate_multipart_subpart4 [part_number=4081]  # not connected
  S5 = Toggle Switch [package=THT]
  IC16 = 4070 4 x 2 Input XOR Gate, multi-part [part_number=4070 package="DIP (Dual Inline) [THT]"]
  IC16_1 = 4070_4_x_2_input_XOR_gate_multipart_subpart2 [part_number=4070]  # not connected
  IC16_4 = 4070_4_x_2_input_XOR_gate_multipart_subpart5 [part_number=4070]  # not connected
  부품11 = 4070_4_x_2_input_XOR_gate_multipart_subpart1 [part_number=4070]  # not connected
  IC17 = 4070 4 x 2 Input XOR Gate, multi-part [part_number=4070 package="DIP (Dual Inline) [THT]"]
  IC17_1 = 4070_4_x_2_input_XOR_gate_multipart_subpart2 [part_number=4070]  # not connected
  IC18_4 = 4070_4_x_2_input_XOR_gate_multipart_subpart5 [part_number=4070]  # not connected
  IC18 = 4070 4 x 2 Input XOR Gate, multi-part [part_number=4070 package="DIP (Dual Inline) [THT]"]
  IC18_1 = 4070_4_x_2_input_XOR_gate_multipart_subpart2 [part_number=4070]  # not connected
  부품13 = 4070_4_x_2_input_XOR_gate_multipart_subpart1 [part_number=4070]  # not connected
  IC20_1 = 4070_4_x_2_input_XOR_gate_multipart_subpart2 [part_number=4070]  # not connected
  IC20 = 4070 4 x 2 Input XOR Gate, multi-part [part_number=4070 package="DIP (Dual Inline) [THT]"]
  IC20_4 = 4070_4_x_2_input_XOR_gate_multipart_subpart5 [part_number=4070]  # not connected
  IC21_1 = 4081_4_x_2_input_AND_gate_multipart_subpart2 [part_number=4081]  # not connected
  IC21 = 4081 4 x 2 Input AND Gate, multi-part [part_number=4081 package="DIP (Dual Inline) [THT]"]
  IC21_4 = 4081_4_x_2_input_AND_gate_multipart_subpart5 [part_number=4081]  # not connected
  IC22 = 4071 4 x 2 Input OR Gate, multi-part [part_number=4071 package="DIP (Dual Inline) [THT]"]
  part = 4071_4_x_2_input_OR_gate_multipart_subpart1 [part_number=4071]  # not connected
  IC22_1 = 4071_4_x_2_input_OR_gate_multipart_subpart2 [part_number=4071]  # not connected

nets:
  N1: IC2.pin1, S1.COM, IC10.connector11, IC12.connector1, IC13.connector4, IC14.connector1, IC21.connector1
  N2: IC2.pin7, IC3.pin7, IC5.connector6, IC7.connector6, IC9.connector6, IC10.connector6, IC11.connector6, IC12.connector6, IC13.connector6, IC14.connector6, IC15.connector6, IC16.connector6, IC17.connector6, IC18.connector6, IC20.connector6, IC21.connector6, IC22.connector6
  N3: IC2.pin12, IC7.connector11, IC9.connector12, IC11.connector8
  N4: IC2.pin13, S2.COM, IC5.connector4, IC7.connector4, IC9.connector1, IC11.connector1, IC22.connector0
  N5: IC2.pin14, IC3.pin14, S1.L2, S2.L2, S3.L2, S4.L2, IC5.connector13, IC7.connector13, IC9.connector13, IC10.connector13, IC11.connector13, IC12.connector13, IC13.connector13, IC14.connector13, IC15.connector13, S5.L2, IC16.connector13, IC17.connector13, IC18.connector13, IC20.connector13, IC21.connector13, IC22.connector13
  N6: IC3.pin1, S3.COM, IC5.connector0, IC9.connector11, IC10.connector12, IC15.connector8, IC22.connector1
  N7: IC3.pin2, IC9.connector0, IC11.connector4, IC15.connector11
  N8: IC3.pin12, IC7.connector5, IC7.connector12, IC15.connector7, IC15.connector12
  N9: IC3.pin13, S4.COM, IC5.connector1, IC5.connector5, IC11.connector0, IC21.connector12
  N10: IC5.connector2, IC11.connector11
  N11: IC5.connector3, IC10.connector0
  N12: IC7.connector3, IC13.connector8
  N13: IC7.connector10, IC10.connector1, IC12.connector12, IC13.connector0
  N14: IC9.connector2, IC13.connector11, IC14.connector0, IC21.connector11
  N15: IC9.connector10, IC12.connector11, IC14.connector12
  N16: IC10.connector2, IC10.connector4
  N17: IC10.connector3, IC16.connector0
  N18: IC10.connector5, IC10.connector10
  N19: IC11.connector2, IC11.connector5
  N20: IC11.connector3, IC17.connector0
  N21: IC11.connector7, IC11.connector10
  N22: IC11.connector9, IC16.connector12
  N23: IC11.connector12, IC13.connector12, IC15.connector10
  N24: IC12.connector0, IC13.connector1, IC14.connector11, IC15.connector9
  N25: IC12.connector2, IC12.connector4
  N26: IC12.connector3, IC18.connector0
  N27: IC12.connector5, IC12.connector9
  N28: IC12.connector7, IC21.connector10
  N29: IC12.connector8, IC12.connector10
  N30: IC13.connector2, IC18.connector12
  N31: IC13.connector3, IC20.connector1
  N32: IC13.connector5, IC13.connector9
  N33: IC13.connector7, IC13.connector10
  N34: IC14.connector2, IC14.connector4
  N35: IC14.connector3, IC20.connector12
  N36: IC14.connector5, IC14.connector10
  N37: S5.COM, IC16.connector1, IC16.connector11, IC17.connector1, IC18.connector1, IC18.connector11, IC20.connector0, IC20.connector11
  N38: IC21.connector0, IC22.connector2

notes:
  A
  B
  C
  D
  not C
  not B
  not A
  a
  b
  c
  d
  f
  not D
  A&B
  A&C
  B&C
  ~A&~B
  ~A&B
  ~A&C
  ~A&~C
  ~B&C
  B&~C
  g
  e
  NOT
  A&~B&C
